# Fritzing sketch EMU v1 fritzing diagram (saved by Fritzing 0.9.3b)
breadboards: 1

parts:
  R2 = Resistor [tolerance=±1% resistance=330k power=0.25W package=THT]
  R3 = Resistor [tolerance=±5% resistance=100k power=0.25W package=THT]
  R1 = Resistor [tolerance=±5% resistance=100k power=0.25W package=THT]
  Q1 = Basic FET P-Channel [package="TO220 [THT]"]
  BATT1 = 4xAA Switchable Battery Pack w/Bare Wire
  Part2 = FC-28 Soil Hygrometer Module - Probe
  Soil_Module = FC-28 Soil Hygrometer Module
  BME280 = BME280 Breakout
  BH1750FVI = BH1750 (GY-302) Breakout Board [part_number=BH1750FVI]
  ADS1115 = Adafruit ADS1115 16Bit I2C ADC [part_number="Adafruit #1085"]
  DS3231SN = ZS-042 RTC Module
  WeMos_D1_Mini1 = WeMos D1 Mini

nets:
  N1: R2.Pin_0, WeMos_D1_Mini1.A0
  N2: R2.Pin_1, Q1.drain, WeMos_D1_Mini1.5V
  VCC: R3.Pin_0, Soil_Module.VCC, BME280.3.3V, BH1750FVI.VCC, ADS1115.VDD, DS3231SN.VCC, WeMos_D1_Mini1.3V3
  N3: R3.Pin_1, WeMos_D1_Mini1.D5
  N4: R1.Pin_0, Q1.gate, DS3231SN.SQW
  N5: R1.Pin_1, Q1.source, BATT1.POS
  GND: BATT1.NEG, Soil_Module.GND, BME280.GND, BH1750FVI.GND, ADS1115.GND, DS3231SN.GND, WeMos_D1_Mini1.G
  N6: Part2.POS, Soil_Module.POS
  N7: Part2.NEG, Soil_Module.NEG
  N8: Soil_Module.AO, ADS1115.AIN0
  N9: BME280.SDI/SDA, BH1750FVI.SDA, ADS1115.SDA, DS3231SN.SDA, WeMos_D1_Mini1.D1
  N10: BME280.SCK/SCL, BH1750FVI.SCL, ADS1115.SCL, DS3231SN.SCL, WeMos_D1_Mini1.D2
  N11: WeMos_D1_Mini1.D0, WeMos_D1_Mini1.RST

custom parts:
  4xAA Switchable Battery Pack w/Bare Wire: 4xAA Switchable Battery Pack with Bare Wire connection
  FC-28 Soil Hygrometer Module - Probe: The FC-28 is a soil hygrometer module that uses the Texas Instruments LM393 comparator chip to provide an analog measurement of soil humidity.
  FC-28 Soil Hygrometer Module: The FC-28 is a soil hygrometer module that uses the Texas Instruments LM393 comparator chip to provide an analog measurement of soil humidity. The digital output is high when soil moisture is over a certain threshold, as determined by adjusting the potentiometer.
  BH1750 (GY-302) Breakout Board: The ROHM Semiconductor BH1750FVI is a digital ambient light sensor for the I2C bus interface. The BH750FVI is able to detect a wide range of light intensities (1-65535 lux). The spectral range is similar to that of the human eye.
  Adafruit ADS1115 16Bit I2C ADC: For microcontrollers without an analog-to-digital converter or when you want a higher-precision ADC, the ADS1115 provides 16-bit precision at 860 samples/second over I2C. The chip can be configured as 4 single-ended input channels, or two differential channels. As a nice bonus, it even includes a programmable gain amplifier, up to x16, to help boost up smaller single/differential signals to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
